// Logisim project EUP5108-Microcontroller.circ as structural Verilog: 23 circuits, main circuit GamingView
module Inverter (
  input  X_i,
  output NotX_o
);

  nand nand_1 (NotX_o, X_i, X_i);
endmodule

module NandFullAddr (
  input  A,
  input  B,
  input  Cin,
  output Sout,
  output Cout
);

  wire U1_out, U2_out, U3_out, U4_out, U5_out, U6_out, U7_out;

  nand U1 (U1_out, A, B);
  nand U2 (U2_out, A, U1_out);
  nand U3 (U3_out, U1_out, B);
  nand U4 (U4_out, U2_out, U3_out);
  nand U5 (U5_out, U4_out, Cin);
  nand U6 (U6_out, U4_out, U5_out);
  nand U7 (U7_out, U5_out, Cin);
  nand U8 (Sout, U6_out, U7_out);
  nand U9 (Cout, U5_out, U1_out);

  // Notes on the sheet:
  //   Nand Gate based 1 Bit Full Adder
endmodule

module NandFullSubtractor (
  input  Bin,
  input  A,
  input  B,
  output D,
  output Bo
);

  wire inverter_1_notx_o, inverter_2_notx_o, inverter_3_notx_o, inverter_4_notx_o, inverter_5_notx_o,
       inverter_6_notx_o, inverter_7_notx_o, nand_1_out, nand_2_out, nand_3_out, nand_4_out, nand_5_out,
       nand_6_out, nand_7_out, nand_8_out, nand_9_out, nand_10_out, nand_11_out, nand_12_out, nand_13_out,
       nand_14_out, nand_15_out, nand_16_out, nand_17_out;

  nand nand_1 (nand_1_out, 1'b1, Bin);
  nand nand_2 (nand_2_out, 1'b1, A);
  nand nand_3 (nand_3_out, 1'b1, B);
  nand nand_4 (nand_4_out, nand_1_out, nand_2_out);
  nand nand_5 (nand_5_out, nand_1_out, A);
  nand nand_6 (nand_6_out, Bin, nand_2_out);
  nand nand_7 (nand_7_out, Bin, A);
  nand nand_8 (nand_8_out, nand_2_out, B);
  nand nand_9 (nand_9_out, Bin, nand_2_out);
  Inverter inverter_1 (.NotX_o(inverter_1_notx_o), .X_i(nand_4_out));
  Inverter inverter_2 (.NotX_o(inverter_2_notx_o), .X_i(nand_5_out));
  Inverter inverter_3 (.NotX_o(inverter_3_notx_o), .X_i(nand_6_out));
  Inverter inverter_4 (.NotX_o(inverter_4_notx_o), .X_i(nand_7_out));
  nand nand_10 (nand_10_out, nand_8_out, nand_9_out);
  nand nand_11 (nand_11_out, inverter_1_notx_o, B);
  nand nand_12 (nand_12_out, inverter_2_notx_o, nand_3_out);
  nand nand_13 (nand_13_out, inverter_3_notx_o, nand_3_out);
  nand nand_14 (nand_14_out, inverter_4_notx_o, B);
  Inverter inverter_5 (.NotX_o(inverter_5_notx_o), .X_i(nand_10_out));
  nand nand_15 (nand_15_out, Bin, B);
  nand nand_16 (nand_16_out, nand_11_out, nand_12_out);
  nand nand_17 (nand_17_out, nand_13_out, nand_14_out);
  nand nand_18 (Bo, inverter_5_notx_o, nand_15_out);
  Inverter inverter_6 (.NotX_o(inverter_6_notx_o), .X_i(nand_16_out));
  Inverter inverter_7 (.NotX_o(inverter_7_notx_o), .X_i(nand_17_out));
  nand nand_19 (D, inverter_6_notx_o, inverter_7_notx_o);
endmodule

module NandFlipFlop (
  input  S,
  input  Clk,
  input  Din,
  input  Reset,
  output Q,
  output QNot
);

  wire nand_1_out, nand_2_out, nand_3_out, nand_4_out;

  nand nand_1 (nand_1_out, S, nand_2_out);
  nand nand_2 (nand_2_out, nand_1_out, Reset, Clk);
  nand nand_3 (nand_3_out, nand_2_out, Clk, nand_4_out);
  nand nand_4 (nand_4_out, nand_3_out, Din);
  nand nand_5 (Q, S, nand_2_out, QNot);
  nand nand_6 (QNot, Q, Reset, nand_3_out);

  // Notes on the sheet:
  //   D Flip Flop a.k.a. 1 bit memory
endmodule

module EUP51_ALU (
  input  Clk,
  input  BnZ,
  input  RetFlags,
  input  StoFlags,
  input  LoadB,
  input  A,
  input  B,
  input  [2:0] FuncSel,
  input  [1:0] AluDst,
  input  [1:0] AluSrc,
  input  Rst,
  output ALU_NotBusy,
  output [2:0] BCnZ_Flags,
  output Result,
  output [1:0] AluDst_o,
  output [1:0] AluSrc_o,
  output ALU_CLK_O
);

  wire and_1_out, and_2_out, and_3_out, and_6_out, and_8_out, d_ff_1_q, d_ff_2_q, d_ff_3_q, d_ff_3_qn,
       d_ff_4_q, inverter_1_notx_o, inverter_2_notx_o, nand_1_out, nand_3_out, nand_4_out,
       nandfulladdr_1_cout, nandfullsubtractor_1_bo, not_1_out, not_3_out, not_4_out, or_2_out, or_3_out,
       or_4_out, or_5_out, or_6_out;
  wire [0:0] register_1_q;
  wire [2:0] bitselector_1_out, multiplexer_1_out, register_3_q;
  wire [3:0] controlled_buffer_1_out, counter_1_q;
  wire [3:3] and_7_out;
  wire [6:1] inverter_3_notx_o;
  wire [7:0] FuncDstSrcLatch_q;

  Register #(.width(1)) register_1 (.D(Result), .en(Result), .clk(ALU_CLK_O), .Q(register_1_q[0]), .clr(Rst));
  and and_1 (and_1_out, FuncDstSrcLatch_q[3], not_1_out);
  or or_1 (ALU_CLK_O, and_3_out, and_2_out);
  and and_2 (and_2_out, ~Rst, and_8_out);  // AND_Gate
  Counter #(.max('hf), .width(4)) counter_1 (
    .count(1'b1), .Q(counter_1_q), .up(1'b1), .clk(and_3_out), .clr(or_2_out));  // open: load, D, carry
  not not_1 (not_1_out, counter_1_q[3]);
  and and_3 (and_3_out, and_1_out, d_ff_3_q, Clk);
  or or_2 (or_2_out, d_ff_3_qn, Rst);
  BitSelector #(.width(2)) bitselector_1 (.in({BnZ, register_1_q[0]}), .out(bitselector_1_out[0]), .sel(LoadB));
  D_Flip_Flop d_ff_1 (.D(nandfulladdr_1_cout), .clk(and_3_out), .Q(d_ff_1_q), .reset(Rst));  // open: Qn, preset
  D_Flip_Flop d_ff_2 (.D(nandfullsubtractor_1_bo), .clk(and_3_out), .Q(d_ff_2_q), .reset(Rst));  // open: Qn, preset
  D_Flip_Flop d_ff_3 (
    .D(FuncDstSrcLatch_q[3]), .clk(FuncDstSrcLatch_q[3]), .Q(d_ff_3_q), .Qn(d_ff_3_qn), .reset(counter_1_q[3]));  // open: preset
  and and_4 (bitselector_1_out[2], d_ff_2_q, FuncDstSrcLatch_q[2], FuncDstSrcLatch_q[1], ~FuncDstSrcLatch_q[0]);  // AND_Gate
  and and_5 (bitselector_1_out[1], d_ff_1_q, FuncDstSrcLatch_q[2], ~FuncDstSrcLatch_q[1], FuncDstSrcLatch_q[0]);  // AND_Gate
  nand nand_1 (nand_1_out, A, B);
  Inverter inverter_1 (.NotX_o(inverter_1_notx_o), .X_i(A));
  Inverter inverter_2 (.NotX_o(inverter_2_notx_o), .X_i(B));
  NandFullAddr nandfulladdr_1 (.Sout(inverter_3_notx_o[5]), .Cout(nandfulladdr_1_cout), .A(A), .B(B), .Cin(d_ff_1_q));
  NandFullSubtractor nandfullsubtractor_1 (
    .D(inverter_3_notx_o[6]), .Bo(nandfullsubtractor_1_bo), .B(B), .Bin(d_ff_2_q), .A(A));
  not not_2 (ALU_NotBusy, d_ff_3_q);
  and and_6 (and_6_out, d_ff_3_qn, ~d_ff_4_q, ~LoadB);  // AND_Gate
  or or_3 (or_3_out, Rst, LoadB);
  nand nand_2 (inverter_3_notx_o[2], inverter_1_notx_o, inverter_2_notx_o);
  nand nand_3 (nand_3_out, inverter_1_notx_o, B);
  nand nand_4 (nand_4_out, inverter_2_notx_o, A);
  not not_3 (not_3_out, d_ff_4_q);
  Multiplexer #(.width(3)) multiplexer_1 (
    .in0(register_3_q), .in1(bitselector_1_out), .out(multiplexer_1_out), .sel(not_3_out), .en(not_3_out));
  nand nand_5 (inverter_3_notx_o[4], nand_3_out, nand_4_out);
  or or_4 (or_4_out, StoFlags, and_6_out);
  Inverter inverter_3 (.NotX_o(inverter_3_notx_o[1]), .X_i(nand_1_out));
  Inverter inverter_4 (.NotX_o(inverter_3_notx_o[3]), .X_i(inverter_3_notx_o[2]));
  Register #(.width(3)) register_2 (
    .D(multiplexer_1_out), .en(or_4_out), .clk(or_4_out), .Q(BCnZ_Flags), .clr(or_3_out));
  LED led_1 (.in(BCnZ_Flags[2]));
  BitSelector bitselector_2 (.in({A, inverter_3_notx_o, 1'b0}), .out(Result), .sel(FuncDstSrcLatch_q[2:0]));
  or or_5 (or_5_out, and_7_out[3], and_8_out);
  LED led_2 (.in(BCnZ_Flags[1]));
  LED led_3 (.in(BCnZ_Flags[0]));
  and and_7 (and_7_out[3], ~and_8_out, or_6_out);  // AND_Gate
  Register FuncDstSrcLatch (
    .D({AluSrc, AluDst, and_7_out[3], FuncSel}), .en(or_5_out), .clk(or_5_out), .Q(FuncDstSrcLatch_q),
    .clr(counter_1_q[3]));
  Register #(.width(3)) register_3 (.D(BCnZ_Flags), .en(StoFlags), .clk(StoFlags), .Q(register_3_q));  // open: clr
  and and_8 (and_8_out, FuncSel[0], FuncSel[1], FuncSel[2]);
  or or_6 (or_6_out, FuncSel[0], FuncSel[1], FuncSel[2]);
  not not_4 (not_4_out, FuncDstSrcLatch_q[3]);
  assign {AluSrc_o, AluDst_o, controlled_buffer_1_out} = not_4_out ? {AluSrc, AluDst, and_7_out[3], FuncSel} : 8'bz;  // Controlled_Buffer controlled_buffer_1
  assign {AluSrc_o, AluDst_o, controlled_buffer_1_out} = FuncDstSrcLatch_q[3] ? FuncDstSrcLatch_q : 8'bz;  // Controlled_Buffer controlled_buffer_2
  D_Flip_Flop d_ff_4 (.D(RetFlags), .clk(RetFlags), .Q(d_ff_4_q), .reset(StoFlags));  // open: Qn, preset

  // Notes on the sheet:
  //   BCnZ_Flags: pull=up
  //   FuncSel: pull=down
  //   AluDst: pull=down
  //   AluSrc: pull=down
  //   AluDst_o: pull=down
  //   AluSrc_o: pull=down
  //   Logical Functions
  //   And
  //   Or
  //   Nor
  //   Xor
  //   Sum
  //   Diff
  //   A
endmodule

module Const8BitValues (
  input  OE,
  input  [3:0] Sel,
  output [7:0] Val
);

  wire [3:0] Consts_data, Consts_data_2;

  assign Val = OE ? {Consts_data_2, Consts_data} : 8'bz;  // Controlled_Buffer controlled_buffer_1
  ROM #(.addrWidth(4)) Consts (.addr(Sel), .data({Consts_data_2, Consts_data}));
  Hex_Digit_Display hex_digit_display_1 (.value(Consts_data_2));  // open: dp
  Hex_Digit_Display hex_digit_display_2 (.value(Consts_data));  // open: dp
  // Probe on {Consts_data_2, Consts_data}

  // Notes on the sheet:
  //   Sel: pull=down
  //   contents of Consts (hex, n*v repeats v):
  //   0 1 2 4 6 8 10 20 40 80 0 0 0 f0 f ff
endmodule

module ALoad8BitCounter (
  input  Load,
  input  [7:0] Byte_i,
  input  Enable,
  input  Inc,
  input  Clr,
  output [7:0] Byte_o
);

  wire and_1_out, not_1_out;

  not not_1 (not_1_out, Load);
  and and_1 (and_1_out, Enable, Inc);
  Counter counter_1 (
    .load(Load), .D(Byte_i), .count(not_1_out), .Q(Byte_o), .up(1'b1), .clk(and_1_out), .clr(Clr));  // open: carry

  // Notes on the sheet:
  //   Inc: pull=down
endmodule

module ALoad16BitCounter (
  input  OElo,
  input  LoadLo,
  input  LoadHi,
  input  [7:0] Byte_i,
  input  OEhi,
  input  Clk,
  input  Dec,
  input  Inc,
  input  Clr,
  output [15:0] Word_o,
  output [3:0] LoByteLoNib_o,
  output [3:0] LoByteHiNib_o,
  output [7:0] Byte_o,
  output [3:0] HiByteLoNib_o,
  output [3:0] HiByteHiNib_o
);

  wire and_1_out, and_2_out, and_3_out, and_4_out, and_5_out, and_6_out, and_7_out, and_8_out, and_9_out,
       and_10_out, and_11_out, and_12_out, and_13_out, and_14_out, and_15_out, and_16_out, and_17_out,
       and_18_out, and_19_out, and_20_out, and_21_out, and_22_out, and_23_out, and_24_out, and_25_out,
       and_26_out, and_27_out, and_28_out, and_29_out, and_30_out, and_31_out, and_32_out, d_ff_1_qn,
       j_k_ff_1_qn, j_k_ff_2_qn, j_k_ff_3_qn, j_k_ff_4_qn, j_k_ff_5_qn, j_k_ff_6_qn, j_k_ff_7_qn,
       j_k_ff_8_qn, j_k_ff_9_qn, j_k_ff_10_qn, j_k_ff_11_qn, j_k_ff_12_qn, j_k_ff_13_qn, j_k_ff_14_qn,
       j_k_ff_15_qn, or_1_out, or_2_out, or_3_out, or_4_out, or_5_out, or_6_out, or_7_out, or_8_out,
       or_9_out, or_10_out, or_11_out, or_12_out, or_13_out, or_14_out, or_15_out, or_16_out;
  wire [7:0] controlled_buffer_6_out, controlled_buffer_7_out, not_8_out, pull_resistor_1_node,
       pull_resistor_2_node, pull_resistor_3_node, register_1_q;

  D_Flip_Flop d_ff_1 (.D(Dec), .clk(Dec), .Qn(d_ff_1_qn), .reset(Inc));  // open: Q, preset
  J_K_Flip_Flop j_k_ff_1 (
    .J(1'b1), .K(1'b1), .clk(Inc), .Q(LoByteLoNib_o[0]), .Qn(j_k_ff_1_qn), .preset(pull_resistor_1_node[0]),
    .reset(pull_resistor_2_node[0]));
  and and_1 (and_1_out, j_k_ff_1_qn, ~d_ff_1_qn);  // AND_Gate
  and and_2 (and_2_out, d_ff_1_qn, LoByteLoNib_o[0]);
  J_K_Flip_Flop j_k_ff_2 (
    .J(or_1_out), .K(or_1_out), .clk(Inc), .Q(LoByteLoNib_o[1]), .Qn(j_k_ff_2_qn),
    .preset(pull_resistor_1_node[1]), .reset(pull_resistor_2_node[1]));
  or or_1 (or_1_out, and_2_out, and_1_out);
  and and_3 (and_3_out, and_2_out, LoByteLoNib_o[1]);
  and and_4 (and_4_out, j_k_ff_2_qn, and_1_out);
  J_K_Flip_Flop j_k_ff_3 (
    .J(or_2_out), .K(or_2_out), .clk(Inc), .Q(LoByteLoNib_o[2]), .Qn(j_k_ff_3_qn),
    .preset(pull_resistor_1_node[2]), .reset(pull_resistor_2_node[2]));
  or or_2 (or_2_out, and_3_out, and_4_out);
  and and_5 (and_5_out, and_3_out, LoByteLoNib_o[2]);
  and and_6 (and_6_out, j_k_ff_3_qn, and_4_out);
  J_K_Flip_Flop j_k_ff_4 (
    .J(or_3_out), .K(or_3_out), .clk(Inc), .Q(LoByteLoNib_o[3]), .Qn(j_k_ff_4_qn),
    .preset(pull_resistor_1_node[3]), .reset(pull_resistor_2_node[3]));
  or or_3 (or_3_out, and_5_out, and_6_out);
  and and_7 (and_7_out, and_5_out, LoByteLoNib_o[3]);
  or or_4 (or_4_out, and_7_out, and_8_out);
  and and_8 (and_8_out, j_k_ff_4_qn, and_6_out);
  Register register_1 (.D(Byte_i), .en(1'b1), .Q(register_1_q), .clk(or_5_out), .clr(Clr));
  or or_5 (or_5_out, LoadLo, LoadHi);
  J_K_Flip_Flop j_k_ff_5 (
    .J(or_4_out), .K(or_4_out), .clk(Inc), .Q(LoByteHiNib_o[0]), .Qn(j_k_ff_5_qn),
    .preset(pull_resistor_1_node[4]), .reset(pull_resistor_2_node[4]));
  Pull_Resistor pull_resistor_1 (.node(pull_resistor_1_node));
  and and_9 (and_9_out, and_7_out, LoByteHiNib_o[0]);
  J_K_Flip_Flop j_k_ff_6 (
    .J(or_6_out), .K(or_6_out), .clk(Inc), .Q(LoByteHiNib_o[1]), .Qn(j_k_ff_6_qn),
    .preset(pull_resistor_1_node[5]), .reset(pull_resistor_2_node[5]));
  or or_6 (or_6_out, and_9_out, and_10_out);
  and and_10 (and_10_out, j_k_ff_5_qn, and_8_out);
  and and_11 (and_11_out, Clk, LoadLo);
  assign pull_resistor_1_node = and_11_out ? register_1_q : 8'bz;  // Controlled_Buffer controlled_buffer_1
  and and_12 (and_12_out, and_9_out, LoByteHiNib_o[1]);
  J_K_Flip_Flop j_k_ff_7 (
    .J(or_7_out), .K(or_7_out), .clk(Inc), .Q(LoByteHiNib_o[2]), .Qn(j_k_ff_7_qn),
    .preset(pull_resistor_1_node[6]), .reset(pull_resistor_2_node[6]));
  or or_7 (or_7_out, and_12_out, and_13_out);
  and and_13 (and_13_out, j_k_ff_6_qn, and_10_out);
  Pull_Resistor pull_resistor_2 (.node(pull_resistor_2_node));
  and and_14 (and_14_out, j_k_ff_7_qn, and_13_out);
  and and_15 (and_15_out, and_12_out, LoByteHiNib_o[2]);
  J_K_Flip_Flop j_k_ff_8 (
    .J(or_8_out), .K(or_8_out), .clk(Inc), .Q(LoByteHiNib_o[3]), .Qn(j_k_ff_8_qn),
    .preset(pull_resistor_1_node[7]), .reset(pull_resistor_2_node[7]));
  or or_8 (or_8_out, and_15_out, and_14_out);
  not not_1 (not_8_out[7], register_1_q[7]);
  not not_2 (not_8_out[6], register_1_q[6]);
  assign pull_resistor_2_node = and_11_out ? not_8_out : 8'bz;  // Controlled_Buffer controlled_buffer_2
  assign pull_resistor_2_node = Clr ? pull_resistor_3_node : 8'bz;  // Controlled_Buffer controlled_buffer_3
  // Probe on Byte_o
  assign Byte_o = OElo ? {LoByteHiNib_o, LoByteLoNib_o} : 8'bz;  // Controlled_Buffer controlled_buffer_4
  assign Byte_o = OEhi ? {HiByteHiNib_o, HiByteLoNib_o} : 8'bz;  // Controlled_Buffer controlled_buffer_5
  and and_16 (and_16_out, Clk, LoadHi);
  not not_3 (not_8_out[5], register_1_q[5]);
  not not_4 (not_8_out[4], register_1_q[4]);
  not not_5 (not_8_out[3], register_1_q[3]);
  not not_6 (not_8_out[2], register_1_q[2]);
  Pull_Resistor #(.pull(1)) pull_resistor_3 (.node(pull_resistor_3_node));
  assign controlled_buffer_6_out = and_16_out ? register_1_q : 8'bz;  // Controlled_Buffer controlled_buffer_6
  and and_17 (and_17_out, and_15_out, LoByteHiNib_o[3]);
  J_K_Flip_Flop j_k_ff_9 (
    .J(or_9_out), .K(or_9_out), .clk(Inc), .Q(HiByteLoNib_o[0]), .Qn(j_k_ff_9_qn),
    .preset(controlled_buffer_6_out[0]), .reset(controlled_buffer_7_out[0]));
  or or_9 (or_9_out, and_17_out, and_18_out);
  and and_18 (and_18_out, j_k_ff_8_qn, and_14_out);
  not not_7 (not_8_out[1], register_1_q[1]);
  not not_8 (not_8_out[0], register_1_q[0]);
  assign controlled_buffer_7_out = and_16_out ? not_8_out : 8'bz;  // Controlled_Buffer controlled_buffer_7
  assign controlled_buffer_7_out = Clr ? pull_resistor_3_node : 8'bz;  // Controlled_Buffer controlled_buffer_8
  Pull_Resistor pull_resistor_4 (.node(controlled_buffer_6_out));
  and and_19 (and_19_out, and_17_out, HiByteLoNib_o[0]);
  J_K_Flip_Flop j_k_ff_10 (
    .J(or_10_out), .K(or_10_out), .clk(Inc), .Q(HiByteLoNib_o[1]), .Qn(j_k_ff_10_qn),
    .preset(controlled_buffer_6_out[1]), .reset(controlled_buffer_7_out[1]));
  or or_10 (or_10_out, and_19_out, and_20_out);
  and and_20 (and_20_out, j_k_ff_9_qn, and_18_out);
  and and_21 (and_21_out, j_k_ff_10_qn, and_20_out);
  Pull_Resistor pull_resistor_5 (.node(controlled_buffer_7_out));
  and and_22 (and_22_out, and_19_out, HiByteLoNib_o[1]);
  J_K_Flip_Flop j_k_ff_11 (
    .J(or_11_out), .K(or_11_out), .clk(Inc), .Q(HiByteLoNib_o[2]), .Qn(j_k_ff_11_qn),
    .preset(controlled_buffer_6_out[2]), .reset(controlled_buffer_7_out[2]));
  or or_11 (or_11_out, and_22_out, and_21_out);
  and and_23 (and_23_out, and_22_out, HiByteLoNib_o[2]);
  and and_24 (and_24_out, j_k_ff_11_qn, and_21_out);
  J_K_Flip_Flop j_k_ff_12 (
    .J(or_12_out), .K(or_12_out), .clk(Inc), .Q(HiByteLoNib_o[3]), .Qn(j_k_ff_12_qn),
    .preset(controlled_buffer_6_out[3]), .reset(controlled_buffer_7_out[3]));
  or or_12 (or_12_out, and_23_out, and_24_out);
  and and_25 (and_25_out, and_23_out, HiByteLoNib_o[3]);
  and and_26 (and_26_out, j_k_ff_12_qn, and_24_out);
  J_K_Flip_Flop j_k_ff_13 (
    .J(or_13_out), .K(or_13_out), .clk(Inc), .Q(HiByteHiNib_o[0]), .Qn(j_k_ff_13_qn),
    .preset(controlled_buffer_6_out[4]), .reset(controlled_buffer_7_out[4]));
  or or_13 (or_13_out, and_25_out, and_26_out);
  and and_27 (and_27_out, and_25_out, HiByteHiNib_o[0]);
  or or_14 (or_14_out, and_27_out, and_28_out);
  and and_28 (and_28_out, j_k_ff_13_qn, and_26_out);
  J_K_Flip_Flop j_k_ff_14 (
    .J(or_14_out), .K(or_14_out), .clk(Inc), .Q(HiByteHiNib_o[1]), .Qn(j_k_ff_14_qn),
    .preset(controlled_buffer_6_out[5]), .reset(controlled_buffer_7_out[5]));
  and and_29 (and_29_out, and_27_out, HiByteHiNib_o[1]);
  J_K_Flip_Flop j_k_ff_15 (
    .J(or_15_out), .K(or_15_out), .clk(Inc), .Q(HiByteHiNib_o[2]), .Qn(j_k_ff_15_qn),
    .preset(controlled_buffer_6_out[6]), .reset(controlled_buffer_7_out[6]));
  or or_15 (or_15_out, and_29_out, and_30_out);
  and and_30 (and_30_out, j_k_ff_14_qn, and_28_out);
  and and_31 (and_31_out, and_29_out, HiByteHiNib_o[2]);
  J_K_Flip_Flop j_k_ff_16 (
    .J(or_16_out), .K(or_16_out), .clk(Inc), .Q(HiByteHiNib_o[3]), .preset(controlled_buffer_6_out[7]),
    .reset(controlled_buffer_7_out[7]));  // open: Qn
  or or_16 (or_16_out, and_31_out, and_32_out);
  and and_32 (and_32_out, j_k_ff_15_qn, and_30_out);

  assign Word_o = {HiByteHiNib_o, HiByteLoNib_o, LoByteHiNib_o, LoByteLoNib_o};

  // Notes on the sheet:
  //   OElo: pull=down
  //   OEhi: pull=down
  //   Word_o: pull=down
  //   Dec: pull=down
endmodule

module ALoad8bitSReg (
  input  [7:0] Byte_i,
  input  S_S,
  input  Load,
  input  S_I,
  input  S_EN,
  input  Clk,
  input  Clr,
  input  OE,
  output S_O,
  output [3:0] LED_lo,
  output [3:0] LED_hi,
  output [7:0] Byte_o,
  output NZero,
  output [7:0] Byte_bo
);

  wire and_1_out, multiplexer_1_out, or_1_out, or_2_out;

  and and_1 (and_1_out, S_S, ~S_EN);  // AND_Gate
  Multiplexer multiplexer_1 (.in0(S_I), .in1(Byte_o[0]), .out(multiplexer_1_out), .sel(and_1_out));  // open: en
  or or_1 (or_1_out, and_1_out, S_EN);
  Shift_Register shift_register_1 (
    .shift(or_1_out), .in(multiplexer_1_out), .clk(or_2_out), .out(Byte_o[0]), .load(Load), .clr(Clr),
    .d0(Byte_i[7]), .q0(Byte_o[7]), .d1(Byte_i[6]), .q1(Byte_o[6]), .d2(Byte_i[5]), .q2(Byte_o[5]),
    .d3(Byte_i[4]), .q3(Byte_o[4]), .d4(Byte_i[3]), .q4(Byte_o[3]), .d5(Byte_i[2]), .q5(Byte_o[2]),
    .d6(Byte_i[1]), .q6(Byte_o[1]), .d7(Byte_i[0]));  // open: q7
  or or_2 (or_2_out, Load, Clk);
  assign Byte_bo = OE ? Byte_o : 8'bz;  // Controlled_Buffer controlled_buffer_1
  LED led_1 (.in(Byte_o[7]));
  LED led_2 (.in(Byte_o[6]));
  LED led_3 (.in(Byte_o[5]));
  LED led_4 (.in(Byte_o[4]));
  LED led_5 (.in(Byte_o[3]));
  LED led_6 (.in(Byte_o[2]));
  LED led_7 (.in(Byte_o[1]));
  LED led_8 (.in(Byte_o[0]));
  or or_3 (NZero, Byte_o[0], Byte_o[1], Byte_o[2], Byte_o[3], Byte_o[4], Byte_o[5], Byte_o[6], Byte_o[7]);

  assign LED_hi = Byte_o[7:4];
  assign LED_lo = Byte_o[3:0];
  assign S_O = Byte_o[0];

  // Notes on the sheet:
  //   OE: pull=down
  //   S_S: pull=down
  //   S_I: pull=down
  //   S_EN: pull=down
endmodule

module ALoad16bitSReg (
  input  S_S,
  input  [7:0] Byte_i,
  input  Load_Lo,
  input  Load_Hi,
  input  S_I,
  input  S_EN,
  input  Clk,
  input  Clr,
  input  OE_Hi,
  input  OE_Lo,
  output S_O,
  output [3:0] LEDHi_lo,
  output [3:0] LEDLo_lo,
  output [3:0] LEDHi_hi,
  output [3:0] LEDLo_hi,
  output [7:0] Byte_bo,
  output [15:0] Word_o
);

  wire and_1_out, multiplexer_1_out, or_1_out, or_2_out, or_3_out;

  and and_1 (and_1_out, S_S, ~S_EN);  // AND_Gate
  Multiplexer multiplexer_1 (.in0(S_I), .in1(LEDLo_lo[0]), .out(multiplexer_1_out), .sel(and_1_out));  // open: en
  or or_1 (or_1_out, and_1_out, S_EN);
  Shift_Register shift_register_1 (
    .shift(or_1_out), .in(multiplexer_1_out), .clk(or_2_out), .out(LEDHi_lo[0]), .load(Load_Hi), .clr(Clr),
    .d0(Byte_i[7]), .q0(LEDHi_hi[3]), .d1(Byte_i[6]), .q1(LEDHi_hi[2]), .d2(Byte_i[5]), .q2(LEDHi_hi[1]),
    .d3(Byte_i[4]), .q3(LEDHi_hi[0]), .d4(Byte_i[3]), .q4(LEDHi_lo[3]), .d5(Byte_i[2]), .q5(LEDHi_lo[2]),
    .d6(Byte_i[1]), .q6(LEDHi_lo[1]), .d7(Byte_i[0]));  // open: q7
  or or_2 (or_2_out, Load_Hi, Clk);
  LED led_1 (.in(LEDHi_hi[1]));
  LED led_2 (.in(LEDHi_hi[0]));
  LED led_3 (.in(LEDHi_hi[3]));
  LED led_4 (.in(LEDHi_hi[2]));
  assign Byte_bo = OE_Hi ? {LEDHi_hi, LEDHi_lo} : 8'bz;  // Controlled_Buffer controlled_buffer_1
  LED led_5 (.in(LEDHi_lo[3]));
  LED led_6 (.in(LEDHi_lo[2]));
  LED led_7 (.in(LEDHi_lo[1]));
  LED led_8 (.in(LEDHi_lo[0]));
  Shift_Register shift_register_2 (
    .shift(or_1_out), .in(LEDHi_lo[0]), .clk(or_3_out), .out(LEDLo_lo[0]), .load(Load_Lo), .clr(Clr),
    .d0(Byte_i[7]), .q0(LEDLo_hi[3]), .d1(Byte_i[6]), .q1(LEDLo_hi[2]), .d2(Byte_i[5]), .q2(LEDLo_hi[1]),
    .d3(Byte_i[4]), .q3(LEDLo_hi[0]), .d4(Byte_i[3]), .q4(LEDLo_lo[3]), .d5(Byte_i[2]), .q5(LEDLo_lo[2]),
    .d6(Byte_i[1]), .q6(LEDLo_lo[1]), .d7(Byte_i[0]));  // open: q7
  or or_3 (or_3_out, Load_Lo, Clk);
  LED led_9 (.in(LEDLo_hi[3]));
  LED led_10 (.in(LEDLo_hi[2]));
  assign Byte_bo = OE_Lo ? {LEDLo_hi, LEDLo_lo} : 8'bz;  // Controlled_Buffer controlled_buffer_2
  LED led_11 (.in(LEDLo_hi[1]));
  LED led_12 (.in(LEDLo_hi[0]));
  LED led_13 (.in(LEDLo_lo[3]));
  LED led_14 (.in(LEDLo_lo[2]));
  LED led_15 (.in(LEDLo_lo[1]));
  LED led_16 (.in(LEDLo_lo[0]));

  assign S_O = LEDLo_lo[0];
  assign Word_o = {LEDHi_hi, LEDHi_lo, LEDLo_hi, LEDLo_lo};

  // Notes on the sheet:
  //   OE_Lo: pull=down
  //   S_S: pull=down
  //   S_I: pull=down
  //   S_EN: pull=down
  //   OE_Hi: pull=down
endmodule

module ALoadSRegWLEDs (
  input  [7:0] Byte_bus,
  input  ExLoad,
  input  ExSel,
  input  Load,
  input  [7:0] Byte_i,
  input  S_S,
  input  S_I,
  input  S_EN,
  input  Clk,
  input  Clr,
  input  OE,
  output S_O,
  output [3:0] LED_lo,
  output [3:0] LED_hi,
  output [7:0] Byte_o,
  output [7:0] Byte_bo
);

  wire and_1_out, multiplexer_1_out, or_1_out, or_2_out, or_3_out;
  wire [7:0] multiplexer_2_out;

  and and_1 (and_1_out, S_S, ~S_EN);  // AND_Gate
  or or_1 (or_1_out, and_1_out, S_EN);
  or or_2 (or_2_out, ExLoad, Load);
  Multiplexer multiplexer_1 (.in0(S_I), .in1(Byte_o[0]), .out(multiplexer_1_out), .sel(and_1_out));  // open: en
  or or_3 (or_3_out, or_2_out, Clk);
  Multiplexer #(.width(8)) multiplexer_2 (
    .in0(Byte_bus), .in1(Byte_i), .out(multiplexer_2_out), .sel(ExSel));  // open: en
  Shift_Register shift_register_1 (
    .shift(or_1_out), .in(multiplexer_1_out), .clk(or_3_out), .out(Byte_o[0]), .load(or_2_out), .clr(Clr),
    .d0(multiplexer_2_out[7]), .q0(Byte_o[7]), .d1(multiplexer_2_out[6]), .q1(Byte_o[6]),
    .d2(multiplexer_2_out[5]), .q2(Byte_o[5]), .d3(multiplexer_2_out[4]), .q3(Byte_o[4]),
    .d4(multiplexer_2_out[3]), .q4(Byte_o[3]), .d5(multiplexer_2_out[2]), .q5(Byte_o[2]),
    .d6(multiplexer_2_out[1]), .q6(Byte_o[1]), .d7(multiplexer_2_out[0]));  // open: q7
  assign Byte_bo = OE ? Byte_o : 8'bz;  // Controlled_Buffer controlled_buffer_1
  LED led_1 (.in(Byte_o[7]));
  Hex_Digit_Display HiNib (.value(Byte_o[7:4]));  // open: dp
  LED led_2 (.in(Byte_o[6]));
  LED led_3 (.in(Byte_o[5]));
  LED led_4 (.in(Byte_o[4]));
  LED led_5 (.in(Byte_o[3]));
  Hex_Digit_Display LoNib (.value(Byte_o[3:0]));  // open: dp
  LED led_6 (.in(Byte_o[2]));
  LED led_7 (.in(Byte_o[1]));
  LED led_8 (.in(Byte_o[0]));

  assign LED_hi = Byte_o[7:4];
  assign LED_lo = Byte_o[3:0];
  assign S_O = Byte_o[0];

  // Notes on the sheet:
  //   S_S: pull=down
  //   S_I: pull=down
  //   S_EN: pull=down
  //   ExLoad: pull=down
  //   ExSel: pull=down
  //   OE: pull=down
endmodule

module ByteProbe (
  input  [7:0] Ni,
  input  [7:0] Si,
  input  [7:0] Ei
);

  Hex_Digit_Display #(.decimalPoint("false")) D1 (.value(Ei[7:4]));
  Hex_Digit_Display #(.decimalPoint("false")) D0 (.value(Ei[3:0]));

  assign Ni = Ei;
  assign Si = Ei;
endmodule

module WordProbe (
  input  [15:0] in_1
);

  Hex_Digit_Display D3 (.value(in_1[15:12]));  // open: dp
  Hex_Digit_Display D2 (.value(in_1[11:8]));  // open: dp
  Hex_Digit_Display D1 (.value(in_1[7:4]));  // open: dp
  Hex_Digit_Display D0 (.value(in_1[3:0]));  // open: dp
endmodule

module DWordProbe (
  input  [31:0] in_1
);

  Hex_Digit_Display #(.decimalPoint("false")) D7 (.value(in_1[31:28]));
  Hex_Digit_Display #(.decimalPoint("false")) D6 (.value(in_1[27:24]));
  Hex_Digit_Display #(.decimalPoint("false")) D5 (.value(in_1[23:20]));
  Hex_Digit_Display #(.decimalPoint("false")) D4 (.value(in_1[19:16]));
  Hex_Digit_Display #(.decimalPoint("false")) D3 (.value(in_1[15:12]));
  Hex_Digit_Display #(.decimalPoint("false")) D2 (.value(in_1[11:8]));
  Hex_Digit_Display #(.decimalPoint("false")) D1 (.value(in_1[7:4]));
  Hex_Digit_Display #(.decimalPoint("false")) D0 (.value(in_1[3:0]));
endmodule

module IDSL (
  input  IRQPend,
  input  [2:0] BCZ,
  input  Rst,
  input  Clk,
  input  ALUNoBusy,
  input  [7:0] Instruction_i,
  output IRLoad,
  output SysHlt,
  output IRQRaise,
  output [2:0] IRQCUM,
  output SysRst,
  output ALURtnFlags,
  output [1:0] TogDRSPBank,
  output ALUStoFlags,
  output IncIP,
  output [1:0] DecIncSP,
  output [15:0] CntlWord
);

  wire and_1_out, and_2_out, and_3_out, and_4_out, and_5_out, and_6_out, d_ff_1_q, decoder_1_out2,
       decoder_1_out6, decoder_1_out7, decoder_1_out11, IPLo_out, not_1_out, not_2_out, or_1_out, or_2_out,
       shift_register_1_q0, shift_register_1_q1, shift_register_1_q2, shift_register_1_q3,
       shift_register_1_q4, shift_register_1_q6, shift_register_1_q7;
  wire [2:0] controlled_buffer_1_out;
  wire [2:1] decoder_1_out8;
  wire [3:3] multiplexer_2_out;
  wire [7:0] counter_1_q, multiplexer_1_out, multiplexer_1_out_2;
  wire [15:0] IRQSeqMap_data, IRSeqMap_data, register_1_q;
  wire [31:0] Sequencer_data;

  WordProbe InsGrid (.in_1({register_1_q[15:8], multiplexer_1_out_2}));
  Register #(.width(16)) register_1 (
    .D({multiplexer_1_out, Instruction_i}), .en(Sequencer_data[0]), .Q(register_1_q), .clk(and_1_out),
    .clr(Rst));
  and and_1 (and_1_out, ALUNoBusy, Clk);
  ROM #(.addrWidth(3), .dataWidth(16)) IRQSeqMap (.addr({decoder_1_out8, IRQPend}), .data(IRQSeqMap_data));
  ROM #(.dataWidth(16)) IRSeqMap (.addr(Instruction_i), .data(IRSeqMap_data));
  ByteProbe byteprobe_1 (.Ei(counter_1_q));  // open: Ni, Si
  ROM #(.dataWidth(32)) Sequencer (
    .addr(counter_1_q), .data({Sequencer_data[31:7], CntlWord[15], Sequencer_data[5:0]}));
  Counter counter_1 (
    .load(Sequencer_data[0]), .D(multiplexer_1_out_2), .count(not_1_out), .Q(counter_1_q), .up(1'b1),
    .clk(and_1_out), .clr(Rst));  // open: carry
  not not_1 (not_1_out, Sequencer_data[0]);
  DWordProbe dwordprobe_1 (.in_1({Sequencer_data[31:7], CntlWord[15], Sequencer_data[5:0]}));
  Multiplexer #(.width(16)) multiplexer_1 (
    .in0(IRSeqMap_data), .in1(IRQSeqMap_data), .out({multiplexer_1_out, multiplexer_1_out_2}), .sel(d_ff_1_q));  // open: en
  // Probe on {multiplexer_1_out, multiplexer_1_out_2}
  // Probe on Sequencer_data[19:16]
  // Probe on register_1_q[15:12]
  // Probe on register_1_q[11:8]
  // Probe on Sequencer_data[23:20]
  // Probe on register_1_q[7:4]
  // Probe on Sequencer_data[27:24]
  // Probe on register_1_q[3:0]
  // Probe on Sequencer_data[31:28]
  D_Flip_Flop d_ff_1 (.D(or_1_out), .clk(or_1_out), .Q(d_ff_1_q), .reset(IRLoad));  // open: Qn, preset
  not not_2 (not_2_out, Sequencer_data[9]);
  or or_1 (or_1_out, IRQPend, decoder_1_out8[2], decoder_1_out8[1]);
  Decoder #(.select(4)) decoder_1 (
    .out1(SysHlt), .out2(decoder_1_out2), .out3(IRQCUM[0]), .out4(IRQCUM[1]), .out5(IRQCUM[2]),
    .out6(decoder_1_out6), .out7(decoder_1_out7), .out8(decoder_1_out8[1]), .out9(decoder_1_out8[2]),
    .out10(SysRst), .out11(decoder_1_out11), .out14(ALURtnFlags), .out15(ALUStoFlags), .sel(CntlWord[11:8]),
    .en(Sequencer_data[7]));  // open: out0, out12, out13
  Multiplexer #(.width(4)) multiplexer_2 (
    .in0(Sequencer_data[19:16]), .in1(register_1_q[15:12]), .out({multiplexer_2_out[3], CntlWord[14:12]}),
    .sel(not_2_out), .en(Sequencer_data[8]));
  Multiplexer #(.width(4)) multiplexer_3 (
    .in0(register_1_q[11:8]), .in1(Sequencer_data[23:20]), .out(CntlWord[11:8]), .sel(Sequencer_data[11]),
    .en(Sequencer_data[10]));
  Multiplexer #(.width(4)) multiplexer_4 (
    .in0(register_1_q[7:4]), .in1(Sequencer_data[27:24]), .out(CntlWord[7:4]), .sel(Sequencer_data[13]),
    .en(or_2_out));
  Multiplexer #(.width(4)) multiplexer_5 (
    .in0(register_1_q[3:0]), .in1(Sequencer_data[31:28]), .out(CntlWord[3:0]), .sel(Sequencer_data[15]),
    .en(Sequencer_data[14]));
  assign controlled_buffer_1_out = register_1_q[15] ? register_1_q[14:12] : 3'bz;  // Controlled_Buffer controlled_buffer_1
  and IPLo (IPLo_out, Sequencer_data[27], ~Sequencer_data[26], ~Sequencer_data[25], ~Sequencer_data[24], Sequencer_data[12]);  // AND_Gate
  Pull_Resistor pull_resistor_1 (.node(CntlWord));
  not not_3 (IRQRaise, decoder_1_out2);
  and and_2 (and_2_out, Sequencer_data[12], ~register_1_q[15]);  // AND_Gate
  and and_3 (and_3_out, controlled_buffer_1_out[2], Sequencer_data[12], BCZ[2]);
  Pull_Resistor pull_resistor_2 (.node(controlled_buffer_1_out));
  and and_4 (and_4_out, IPLo_out, ~or_2_out);  // AND_Gate
  or or_2 (or_2_out, and_2_out, and_3_out, and_5_out, and_6_out);
  and and_5 (and_5_out, controlled_buffer_1_out[1], Sequencer_data[12], BCZ[1]);
  and and_6 (and_6_out, controlled_buffer_1_out[0], Sequencer_data[12], BCZ[0]);
  Shift_Register #(.length(9)) shift_register_1 (
    .clk(and_1_out), .out(IRLoad), .load(and_1_out), .clr(Rst), .d0(and_4_out), .q0(shift_register_1_q0),
    .d1(Sequencer_data[5]), .q1(shift_register_1_q1), .d2(decoder_1_out7), .q2(shift_register_1_q2),
    .d3(Sequencer_data[4]), .q3(shift_register_1_q3), .d4(decoder_1_out6), .q4(shift_register_1_q4),
    .d5(Sequencer_data[3]), .q5(TogDRSPBank[1]), .d6(Sequencer_data[2]), .q6(shift_register_1_q6),
    .d7(Sequencer_data[1]), .q7(shift_register_1_q7), .d8(Sequencer_data[0]));  // open: shift, in, q8
  or or_3 (TogDRSPBank[0], shift_register_1_q6, decoder_1_out11);
  or or_4 (IncIP, shift_register_1_q7, shift_register_1_q0);
  or or_5 (DecIncSP[0], shift_register_1_q4, shift_register_1_q3);
  or or_6 (DecIncSP[1], shift_register_1_q2, shift_register_1_q1);

  // Notes on the sheet:
  //   IRQPend: pull=down
  //   contents of IRQSeqMap (hex, n*v repeats v):
  //   0 2c0 3c0 2c0 4c0 2c0 3c0 2c0
  //   contents of IRSeqMap (hex, n*v repeats v):
  //   15 f0 0 13*65 0 115 b15 13*42 0 a0 215 13*4c 6a 24 11 315 12*48 6a 24 11 48 415 11*48 6a 24 11 48 48
  //   515 10*48 6a 24 11 48 48 48 68a 5*48 4*1290 6a 24 11 48 48 48 b0 715 4*48 4*0 60 a060 9060 c060 48
  //   48 0 0 3c0 6472 6872 6c82 5072 5472 5872 5c82 56 a056 9056 c056 48 df 50 18 6172 915 6972 6d82 5172
  //   5572 5972 5d82 6a 24 11 5*48 6272 6672 a15 6e82 5272 5672 5a72 5e82 6a 24 11 5*48 6270 6670 6e80
  //   2292 5270 5670 5e80 5f82 6a 24 11 48 48 48 1292 7072 1272 1472 2272 2472 4272 4472 3072 3470 6a 24
  //   11 48 48 48 1692 7572 1172 1672 2172 2672 4172 4672 3172 3a70 6a 24 11 48 48 48 2692 7a72 130 134
  //   138 f30 f34 f38 1298 3c70 6a 24 11 48 48 48 1698 7f72 30 34 38 3c
  //   contents of Sequencer (hex, n*v repeats v):
  //   300f000 400f000 600f000 700f000 800f000 900f000 f0cc00 af0fc00 bf0fc00 1000c000 1500f000 1000c002
  //   1900f000 5000c000 5800f000 1000c000 1000c001 1000c00a 1000d000 1000c008 1000c001 1000c482 1000c001 0
  //   2000c024 2900f000 2000c020 2800f000 1000c004 1000c002 1000c000 1000c002 1000c000 1000c002 1000c000
  //   1000c001 4002 5000 1000c002 1000c001 8*0 440 3003400 1000c002 1000c001 440 4003400 1000c002 1000c001
  //   440 5003400 1000c002 1000c001 440 6003400 7003400 1000c002 1000c001 0 4006 2007000 1000c004 1060cc80
  //   1000c020 1000c001 4000 5002 1000c000 1000c001 4008 1007002 1000c008 1000c001 8000c004 8200f000
  //   9000c010 9200f020 14 20 1000c002 1500f000 1000c002 1900f000 5000c000 5800f000 1000c000 1000c001 0 0
  //   1000c002 1000c300 1800f300 1000c001 0 4002 2007000 1000c000 1000c001 0 2000c000 2000d002 1000c000
  //   1000c001 0 0 100c00 510fc00 440 1000c502 1000c001 11*0 100c00 510fc00 440 500 0 5003c02 e00c02
  //   10e0cd00 1000c001 0 1000c482 1000c020 1000c001 0 0 0 4000 3007000 1000c002 1500f000 440 1000c502
  //   1000c001 0 1000c002 1500f000 500c40 530f00 440 1000c502 1000c001 0 b000c000 b500f000 7000c000
  //   7b00f000 5000c000 5700f000 a000c000 a500f000 6000c000 6a00f000 5000c000 5600f000 1000c002 1000c001 0
  //   0 1000c002 1600f000 1000c002 1700f000 1000c002 1000c001 10*0 8000c004 8200f000 9000c010 9200f020
  //   6000c010 6200f020 7000c010 7200f020 5000c010 5200f020 4000c010 4200f020 3000c010 3200f020 f00c94 20
  //   900f000 400 800f400 1000c000 1500f000 1000c002 1900f000 5000c000 5800f000 1000c000 1000c001 4*0
  //   2000c024 2300f000 2000c020 2400f000 2000c020 2500f000 2000c020 2700f000 2000c020 2600f000 2000c020
  //   2900f000 2000c020 2800f000 10e0cc84 1000c002 10f0cc81 a000c000 a600f000 b000c000 b700f000 1000c002
  //   1000c000 1500f000 e00c40 e50f00 0 5003c00 e00c00 e50f02 1000c001
endmodule

module EUP5108 (
  input  Rst,
  input  StopStart_i,
  input  Step1,
  input  Step1En_i,
  input  IRQ,
  input  [1:0] S_Cntl_In,
  input  P0el,
  input  P0es,
  input  P1el,
  input  P1es,
  input  P2el,
  input  P2es,
  input  P3el,
  input  P3es,
  input  [7:0] P1bi,
  input  [7:0] P2bi,
  input  [7:0] P3bi,
  input  [7:0] P0bi,
  output RS,
  output Clk,
  output S_O,
  output P0oe,
  output P0l,
  output P1oe,
  output P1l,
  output P2oe,
  output P2l,
  output P3oe,
  output P3l,
  output [7:0] P1bo,
  output [7:0] P2bo,
  output [7:0] P3bo,
  output [7:0] P0bo
);

  wire aload8bitsreg_1_s_o, aload8bitsreg_2_nzero, aload8bitsreg_2_s_o, aload8bitsreg_3_s_o,
       aload16bitsreg_1_s_o, and_1_out, and_2_out, and_4_out, and_5_out, and_6_out, button_1_out,
       clock_1_out, d_ff_1_q, d_ff_2_q, decoder_1_out0, decoder_1_out1, decoder_1_out2, decoder_1_out3,
       decoder_2_out0, decoder_2_out1, decoder_2_out2, decoder_2_out3, decoder_3_out8, decoder_3_out9,
       decoder_3_out10, decoder_3_out11, decoder_4_out0, decoder_4_out8, decoder_4_out9, decoder_4_out10,
       decoder_4_out11, eup51_alu_1_alu_clk_o, eup51_alu_1_alu_notbusy, eup51_alu_1_result,
       idsl_1_alurtnflags, idsl_1_alustoflags, idsl_1_incip, idsl_1_irload, idsl_1_irqraise, idsl_1_syshlt,
       idsl_1_sysrst, multiplexer_1_out, multiplexer_2_out, or_1_out, or_2_out, or_3_out, or_4_out,
       pull_resistor_1_node, pull_resistor_2_node, shift_register_1_q0, t_ff_2_q, t_ff_2_qn, t_ff_3_q,
       t_ff_3_qn;
  wire [1:0] decoder_3_out3, eup51_alu_1_aludst_o, eup51_alu_1_alusrc_o, idsl_1_decincsp, idsl_1_togdrspbank,
       shift_register_1_q5, shift_register_1_q7;
  wire [2:0] eup51_alu_1_bcnz_flags, idsl_1_irqcum, shift_register_1_q3;
  wire [3:0] aload8bitsreg_1_led_hi, aload8bitsreg_1_led_lo, aload8bitsreg_2_led_hi, aload8bitsreg_2_led_lo,
       aload8bitsreg_3_led_hi, aload8bitsreg_3_led_lo, aload8bitsreg_4_led_hi, aload8bitsreg_4_led_lo,
       aload16bitcounter_1_hibytehinib_o, aload16bitcounter_1_hibytelonib_o,
       aload16bitcounter_1_lobytehinib_o, aload16bitcounter_1_lobytelonib_o,
       aload16bitcounter_2_hibytehinib_o, aload16bitcounter_2_hibytelonib_o,
       aload16bitcounter_2_lobytehinib_o, aload16bitcounter_2_lobytelonib_o, aload16bitsreg_1_ledhi_hi,
       aload16bitsreg_1_ledhi_lo, aload16bitsreg_1_ledlo_hi, aload16bitsreg_1_ledlo_lo, decoder_3_out4,
       decoder_3_out6, decoder_4_out1, shift_register_1_out, shift_register_1_q11;
  wire [7:0] aload8bitsreg_1_byte_bo, DRAM_dout, EEPROM_dout;
  wire [15:0] aload16bitcounter_1_word_o, aload16bitcounter_2_word_o, aload16bitsreg_1_word_o,
       controlled_buffer_1_out, controlled_buffer_3_out, idsl_1_cntlword;
  wire [23:0] counter_1_q;

  Decoder #(.enable("false"), .select(2)) decoder_1 (
    .out0(decoder_1_out0), .out1(decoder_1_out1), .out2(decoder_1_out2), .out3(decoder_1_out3),
    .sel(eup51_alu_1_aludst_o));
  Hex_Digit_Display #(.decimalPoint("false")) hex_digit_display_1 (.value(aload8bitsreg_1_led_hi));
  Hex_Digit_Display #(.decimalPoint("false")) hex_digit_display_2 (.value(aload8bitsreg_2_led_hi));
  Multiplexer #(.select(2)) multiplexer_1 (
    .in0(aload8bitsreg_1_s_o), .in1(aload8bitsreg_2_s_o), .in2(aload8bitsreg_3_s_o),
    .in3(aload16bitsreg_1_s_o), .out(multiplexer_1_out), .sel(eup51_alu_1_aludst_o));  // open: en
  Hex_Digit_Display #(.decimalPoint("false")) hex_digit_display_3 (.value(aload8bitsreg_1_led_lo));
  ALoad8bitSReg aload8bitsreg_1 (
    .Byte_bo(aload8bitsreg_1_byte_bo), .S_O(aload8bitsreg_1_s_o), .LED_lo(aload8bitsreg_1_led_lo),
    .LED_hi(aload8bitsreg_1_led_hi), .OE(decoder_3_out3[1]), .S_S(decoder_2_out0), .S_I(eup51_alu_1_result),
    .S_EN(decoder_1_out0), .Clk(eup51_alu_1_alu_clk_o), .Load(decoder_3_out3[0]),
    .Byte_i(aload8bitsreg_1_byte_bo), .Clr(or_1_out));  // open: Byte_o, NZero
  Hex_Digit_Display #(.decimalPoint("false")) hex_digit_display_4 (.value(aload8bitsreg_2_led_lo));
  ALoad8bitSReg aload8bitsreg_2 (
    .Byte_bo(aload8bitsreg_1_byte_bo), .S_O(aload8bitsreg_2_s_o), .LED_lo(aload8bitsreg_2_led_lo),
    .LED_hi(aload8bitsreg_2_led_hi), .NZero(aload8bitsreg_2_nzero), .OE(decoder_3_out4[1]),
    .S_S(decoder_2_out1), .S_I(eup51_alu_1_result), .S_EN(decoder_1_out1), .Clk(eup51_alu_1_alu_clk_o),
    .Load(decoder_3_out4[0]), .Byte_i(aload8bitsreg_1_byte_bo), .Clr(or_1_out));  // open: Byte_o
  EUP51_ALU eup51_alu_1 (
    .Result(eup51_alu_1_result), .AluSrc_o(eup51_alu_1_alusrc_o), .AluDst_o(eup51_alu_1_aludst_o),
    .BCnZ_Flags(eup51_alu_1_bcnz_flags), .ALU_CLK_O(eup51_alu_1_alu_clk_o),
    .ALU_NotBusy(eup51_alu_1_alu_notbusy), .RetFlags(idsl_1_alurtnflags), .StoFlags(idsl_1_alustoflags),
    .FuncSel(shift_register_1_q3), .AluDst(shift_register_1_q5), .AluSrc(shift_register_1_q7), .Clk(Clk),
    .BnZ(aload8bitsreg_2_nzero), .LoadB(decoder_3_out4[0]), .Rst(shift_register_1_q0), .A(multiplexer_1_out),
    .B(multiplexer_2_out));
  Multiplexer #(.select(2)) multiplexer_2 (
    .in0(aload8bitsreg_1_s_o), .in1(aload8bitsreg_2_s_o), .in2(aload8bitsreg_3_s_o),
    .in3(aload16bitsreg_1_s_o), .out(multiplexer_2_out), .sel(eup51_alu_1_alusrc_o));  // open: en
  Decoder #(.enable("false"), .select(2)) decoder_2 (
    .out0(decoder_2_out0), .out1(decoder_2_out1), .out2(decoder_2_out2), .out3(decoder_2_out3),
    .sel(eup51_alu_1_alusrc_o));
  // Probe on shift_register_1_q3
  Const8BitValues const8bitvalues_1 (
    .Val(aload8bitsreg_1_byte_bo), .OE(decoder_4_out0), .Sel({shift_register_1_q5, shift_register_1_q7}));
  // Probe on aload8bitsreg_1_byte_bo
  LED #(.active("false")) led_1 (.in(eup51_alu_1_alu_notbusy));
  Hex_Digit_Display #(.decimalPoint("false")) hex_digit_display_5 (.value(aload16bitsreg_1_ledhi_hi));
  Hex_Digit_Display #(.decimalPoint("false")) hex_digit_display_6 (.value(aload16bitsreg_1_ledhi_lo));
  Hex_Digit_Display #(.decimalPoint("false")) hex_digit_display_7 (.value(aload8bitsreg_3_led_hi));
  Hex_Digit_Display #(.decimalPoint("false")) hex_digit_display_8 (.value(aload8bitsreg_3_led_lo));
  Shift_Register #(.length(16)) shift_register_1 (
    .shift(1'b0), .clk(Clk), .out(shift_register_1_out[0]), .load(1'b1), .clr(or_1_out),
    .d0(idsl_1_cntlword[15]), .q0(shift_register_1_q0), .d1(idsl_1_cntlword[14]),
    .q1(shift_register_1_q3[2]), .d2(idsl_1_cntlword[13]), .q2(shift_register_1_q3[1]),
    .d3(idsl_1_cntlword[12]), .q3(shift_register_1_q3[0]), .d4(idsl_1_cntlword[11]),
    .q4(shift_register_1_q5[1]), .d5(idsl_1_cntlword[10]), .q5(shift_register_1_q5[0]),
    .d6(idsl_1_cntlword[9]), .q6(shift_register_1_q7[1]), .d7(idsl_1_cntlword[8]),
    .q7(shift_register_1_q7[0]), .d8(idsl_1_cntlword[7]), .q8(shift_register_1_q11[3]),
    .d9(idsl_1_cntlword[6]), .q9(shift_register_1_q11[2]), .d10(idsl_1_cntlword[5]),
    .q10(shift_register_1_q11[1]), .d11(idsl_1_cntlword[4]), .q11(shift_register_1_q11[0]),
    .d12(idsl_1_cntlword[3]), .q12(shift_register_1_out[3]), .d13(idsl_1_cntlword[2]),
    .q13(shift_register_1_out[2]), .d14(idsl_1_cntlword[1]), .q14(shift_register_1_out[1]),
    .d15(idsl_1_cntlword[0]));  // open: in, q15
  Hex_Digit_Display #(.decimalPoint("false")) hex_digit_display_9 (.value(aload16bitsreg_1_ledlo_hi));
  Hex_Digit_Display #(.decimalPoint("false")) hex_digit_display_10 (.value(aload16bitsreg_1_ledlo_lo));
  ALoad8bitSReg aload8bitsreg_3 (
    .Byte_bo(aload8bitsreg_1_byte_bo), .S_O(aload8bitsreg_3_s_o), .LED_lo(aload8bitsreg_3_led_lo),
    .LED_hi(aload8bitsreg_3_led_hi), .OE(decoder_3_out4[3]), .S_S(decoder_2_out2), .S_I(eup51_alu_1_result),
    .S_EN(decoder_1_out2), .Clk(eup51_alu_1_alu_clk_o), .Load(decoder_3_out4[2]),
    .Byte_i(aload8bitsreg_1_byte_bo), .Clr(or_1_out));  // open: Byte_o, NZero
  WordProbe wordprobe_1 (.in_1(idsl_1_cntlword));
  Decoder #(.enable("false"), .select(4)) decoder_3 (
    .out1(decoder_4_out1[1]), .out2(decoder_4_out1[2]), .out3(decoder_3_out3[0]), .out4(decoder_3_out4[0]),
    .out5(decoder_3_out4[2]), .out6(decoder_3_out6[0]), .out7(decoder_3_out6[1]), .out8(decoder_3_out8),
    .out9(decoder_3_out9), .out10(decoder_3_out10), .out11(decoder_3_out11), .out12(P0l), .out13(P1l),
    .out14(P2l), .out15(P3l), .sel(shift_register_1_q11));  // open: out0
  Decoder #(.enable("false"), .select(4)) decoder_4 (
    .out0(decoder_4_out0), .out1(decoder_4_out1[0]), .out2(decoder_4_out1[3]), .out3(decoder_3_out3[1]),
    .out4(decoder_3_out4[1]), .out5(decoder_3_out4[3]), .out6(decoder_3_out6[3]), .out7(decoder_3_out6[2]),
    .out8(decoder_4_out8), .out9(decoder_4_out9), .out10(decoder_4_out10), .out11(decoder_4_out11),
    .out12(P0oe), .out13(P1oe), .out14(P2oe), .out15(P3oe), .sel(shift_register_1_out));
  ALoad16bitSReg aload16bitsreg_1 (
    .Word_o(aload16bitsreg_1_word_o), .LEDLo_hi(aload16bitsreg_1_ledlo_hi), .S_O(aload16bitsreg_1_s_o),
    .LEDHi_hi(aload16bitsreg_1_ledhi_hi), .OE_Lo(decoder_3_out6[3]), .S_I(eup51_alu_1_result),
    .Clk(eup51_alu_1_alu_clk_o), .Clr(or_1_out), .Byte_i(aload8bitsreg_1_byte_bo), .OE_Hi(decoder_3_out6[2]),
    .Load_Hi(decoder_3_out6[1]), .S_EN(decoder_1_out3), .S_S(decoder_2_out3), .Load_Lo(decoder_3_out6[0]),
    .LEDHi_lo(aload16bitsreg_1_ledhi_lo), .Byte_bo(aload8bitsreg_1_byte_bo),
    .LEDLo_lo(aload16bitsreg_1_ledlo_lo));
  ALoadSRegWLEDs aloadsregwleds_1 (
    .ExSel(P0es), .S_I(S_Cntl_In[1]), .S_O(S_O), .S_EN(S_Cntl_In[0]), .Byte_bo(aload8bitsreg_1_byte_bo),
    .Byte_o(P0bo), .ExLoad(P0el), .Load(P0l), .Clr(or_1_out), .Byte_bus(aload8bitsreg_1_byte_bo),
    .Byte_i(P0bi), .OE(P0oe));  // open: LED_hi, S_S, LED_lo, Clk
  or or_1 (or_1_out, Rst, idsl_1_sysrst);
  IDSL idsl_1 (
    .IRQCUM(idsl_1_irqcum), .IRLoad(idsl_1_irload), .ALURtnFlags(idsl_1_alurtnflags), .IRQPend(d_ff_1_q),
    .Rst(or_1_out), .ALUStoFlags(idsl_1_alustoflags), .TogDRSPBank(idsl_1_togdrspbank),
    .SysRst(idsl_1_sysrst), .IRQRaise(idsl_1_irqraise), .DecIncSP(idsl_1_decincsp),
    .BCZ(eup51_alu_1_bcnz_flags), .Clk(Clk), .CntlWord(idsl_1_cntlword), .IncIP(idsl_1_incip),
    .SysHlt(idsl_1_syshlt), .ALUNoBusy(eup51_alu_1_alu_notbusy), .Instruction_i(EEPROM_dout));
  Hex_Digit_Display #(.decimalPoint("false")) hex_digit_display_11 (.value(aload16bitcounter_1_hibytehinib_o));
  Hex_Digit_Display #(.decimalPoint("false")) hex_digit_display_12 (.value(aload16bitcounter_2_hibytehinib_o));
  ALoadSRegWLEDs aloadsregwleds_2 (
    .S_S(1'b0), .ExSel(P1es), .S_EN(1'b0), .Byte_bo(aload8bitsreg_1_byte_bo), .Byte_o(P1bo), .ExLoad(P1el),
    .Load(P1l), .Clr(or_1_out), .Byte_bus(aload8bitsreg_1_byte_bo), .Byte_i(P1bi), .OE(P1oe));  // open: LED_hi, S_I, LED_lo, S_O, Clk
  Hex_Digit_Display #(.decimalPoint("false")) hex_digit_display_13 (.value(aload8bitsreg_4_led_hi));
  Hex_Digit_Display #(.decimalPoint("false")) hex_digit_display_14 (.value(aload8bitsreg_4_led_lo));
  Hex_Digit_Display #(.decimalPoint("false")) hex_digit_display_15 (.value(aload16bitcounter_1_hibytelonib_o));
  Hex_Digit_Display #(.decimalPoint("false")) hex_digit_display_16 (.value(aload16bitcounter_1_lobytehinib_o));
  Hex_Digit_Display #(.decimalPoint("false")) hex_digit_display_17 (.value(aload16bitcounter_2_hibytelonib_o));
  Hex_Digit_Display #(.decimalPoint("false")) hex_digit_display_18 (.value(aload16bitcounter_2_lobytehinib_o));
  Pull_Resistor #(.pull(1)) pull_resistor_1 (.node(pull_resistor_1_node));
  // Switch No_Halt: pin names not known; wires that end beside it: 1'b0, pull_resistor_1_node
  T_Flip_Flop t_ff_1 (.T(or_2_out), .clk(or_2_out), .Qn(RS), .reset(or_1_out));  // open: Q, preset
  or or_2 (or_2_out, and_1_out, and_2_out, StopStart_i);
  and and_1 (and_1_out, idsl_1_syshlt, ~StopStart_i, pull_resistor_1_node);  // AND_Gate
  and and_2 (and_2_out, idsl_1_irload, ~Step1, Step1En_i);  // AND_Gate
  ALoad8bitSReg aload8bitsreg_4 (
    .LED_lo(aload8bitsreg_4_led_lo), .LED_hi(aload8bitsreg_4_led_hi), .Load(idsl_1_irload),
    .Byte_i(EEPROM_dout), .Clr(or_1_out));  // open: Byte_o, Byte_bo, S_O, NZero, OE, S_S, S_I, S_EN, Clk
  Hex_Digit_Display #(.decimalPoint("false")) hex_digit_display_19 (.value(aload16bitcounter_1_lobytelonib_o));
  ALoad16BitCounter aload16bitcounter_1 (
    .LoByteHiNib_o(aload16bitcounter_1_lobytehinib_o), .Byte_o(aload8bitsreg_1_byte_bo),
    .HiByteHiNib_o(aload16bitcounter_1_hibytehinib_o), .LoByteLoNib_o(aload16bitcounter_1_lobytelonib_o),
    .HiByteLoNib_o(aload16bitcounter_1_hibytelonib_o), .Word_o(aload16bitcounter_1_word_o), .Clk(Clk),
    .LoadLo(decoder_3_out8), .LoadHi(decoder_3_out9), .OElo(decoder_4_out8), .OEhi(decoder_4_out9),
    .Clr(or_1_out), .Inc(idsl_1_incip), .Byte_i(aload8bitsreg_1_byte_bo));  // open: Dec
  Hex_Digit_Display #(.decimalPoint("false")) hex_digit_display_20 (.value(aload16bitcounter_2_lobytelonib_o));
  ALoad16BitCounter aload16bitcounter_2 (
    .LoByteHiNib_o(aload16bitcounter_2_lobytehinib_o), .Byte_o(aload8bitsreg_1_byte_bo),
    .HiByteHiNib_o(aload16bitcounter_2_hibytehinib_o), .LoByteLoNib_o(aload16bitcounter_2_lobytelonib_o),
    .HiByteLoNib_o(aload16bitcounter_2_hibytelonib_o), .Word_o(aload16bitcounter_2_word_o), .Clk(Clk),
    .LoadLo(decoder_3_out10), .LoadHi(decoder_3_out11), .OElo(decoder_4_out10), .OEhi(decoder_4_out11),
    .Clr(or_1_out), .Inc(idsl_1_decincsp[1]), .Dec(idsl_1_decincsp[0]), .Byte_i(aload8bitsreg_1_byte_bo));
  and and_3 (Clk, RS, ~or_1_out, clock_1_out);  // AND_Gate
  T_Flip_Flop t_ff_2 (
    .T(idsl_1_togdrspbank[0]), .clk(idsl_1_togdrspbank[0]), .Q(t_ff_2_q), .Qn(t_ff_2_qn), .reset(or_1_out));  // open: preset
  ALoadSRegWLEDs aloadsregwleds_3 (
    .S_S(1'b0), .ExSel(P2es), .S_EN(1'b0), .Byte_bo(aload8bitsreg_1_byte_bo), .Byte_o(P2bo), .ExLoad(P2el),
    .Load(P2l), .Clr(or_1_out), .Byte_bus(aload8bitsreg_1_byte_bo), .Byte_i(P2bi), .OE(P2oe));  // open: LED_hi, S_I, LED_lo, S_O, Clk
  Clock clock_1 (.out(clock_1_out));
  LED led_2 (.in(Clk));
  and and_4 (and_4_out, d_ff_1_q, idsl_1_irload);
  or or_3 (or_3_out, and_4_out, or_1_out, idsl_1_irqcum[0]);
  LED led_3 (.in(t_ff_2_q));
  LED led_4 (.in(t_ff_2_qn));
  assign controlled_buffer_1_out = t_ff_2_q ? aload16bitcounter_2_word_o : 16'bz;  // Controlled_Buffer controlled_buffer_1
  assign controlled_buffer_1_out = t_ff_2_qn ? aload16bitsreg_1_word_o : 16'bz;  // Controlled_Buffer controlled_buffer_2
  D_Flip_Flop d_ff_1 (.D(and_5_out), .clk(and_5_out), .Q(d_ff_1_q), .reset(or_3_out));  // open: Qn, preset
  assign controlled_buffer_3_out = t_ff_3_qn ? aload16bitcounter_1_word_o : 16'bz;  // Controlled_Buffer controlled_buffer_3
  LED led_5 (.in(t_ff_3_qn));
  T_Flip_Flop t_ff_3 (
    .T(idsl_1_togdrspbank[1]), .clk(idsl_1_togdrspbank[1]), .Q(t_ff_3_q), .Qn(t_ff_3_qn), .reset(or_1_out));  // open: preset
  LED led_6 (.in(t_ff_3_q));
  assign controlled_buffer_3_out = t_ff_3_q ? controlled_buffer_1_out : 16'bz;  // Controlled_Buffer controlled_buffer_4
  ALoadSRegWLEDs aloadsregwleds_4 (
    .S_S(1'b0), .ExSel(P3es), .S_EN(1'b0), .Byte_bo(aload8bitsreg_1_byte_bo), .Byte_o(P3bo), .ExLoad(P3el),
    .Load(P3l), .Clr(or_1_out), .Byte_bus(aload8bitsreg_1_byte_bo), .Byte_i(P3bi), .OE(P3oe));  // open: LED_hi, S_I, LED_lo, S_O, Clk
  // Probe on counter_1_q
  Counter #(.max('hffffff), .width(24)) counter_1 (
    .Q(counter_1_q), .clk(Clk), .clr(button_1_out));  // open: load, D, count, carry, up
  Button button_1 (.out(button_1_out));
  RAM #(.addrWidth(16), .enables("line"), .\type ("nonvolatile")) EEPROM (
    .addr(controlled_buffer_3_out), .we(pull_resistor_2_node), .clk(Clk), .din(aload8bitsreg_1_byte_bo),
    .dout(EEPROM_dout));
  RAM #(.addrWidth(16), .enables("line")) DRAM (
    .addr(controlled_buffer_1_out), .we(decoder_4_out1[2]), .clk(Clk), .din(aload8bitsreg_1_byte_bo),
    .dout(DRAM_dout));
  and and_5 (and_5_out, ~and_6_out, d_ff_2_q);  // AND_Gate
  D_Flip_Flop d_ff_2 (.D(1'b0), .clk(1'b0), .Q(d_ff_2_q), .preset(idsl_1_irqcum[1]), .reset(or_4_out));  // open: Qn
  or or_4 (or_4_out, or_1_out, idsl_1_irqcum[2]);
  Pull_Resistor pull_resistor_2 (.node(pull_resistor_2_node));
  // Switch switch_1: pin names not known; wires that end beside it: decoder_4_out1[1], pull_resistor_2_node
  and and_6 (and_6_out, idsl_1_irqraise, IRQ);
  Pull_Resistor #(.pull(1)) pull_resistor_3 (.node(IRQ));
  ByteProbe byteprobe_1 (.Si(EEPROM_dout));  // open: Ni, Ei
  ByteProbe byteprobe_2 (.Ni(DRAM_dout));  // open: Si, Ei
  assign aload8bitsreg_1_byte_bo = decoder_4_out1[0] ? EEPROM_dout : 8'bz;  // Controlled_Buffer controlled_buffer_5
  assign aload8bitsreg_1_byte_bo = decoder_4_out1[3] ? DRAM_dout : 8'bz;  // Controlled_Buffer controlled_buffer_6

  // Notes on the sheet:
  //   P2es: pull=down
  //   P2bi: pull=down
  //   P3el: pull=down
  //   P3es: pull=down
  //   P3bi: pull=down
  //   StopStart_i: pull=down
  //   Step1: pull=up
  //   Step1En_i: pull=down
  //   IRQ: pull=up
  //   S_Cntl_In: pull=down
  //   P0el: pull=down
  //   P0l: pull=down
  //   P0es: pull=down
  //   P0bi: pull=down
  //   P1el: pull=down
  //   P1es: pull=down
  //   P1bi: pull=down
  //   P2el: pull=down
  //   A reg
  //   B reg
  //   (3)
  //   (4)
  //   (7)
  //   (5)
  //   T reg
  //   Load Location
  //   (6)
  //   Data Register
  //   (c)
  //   OE Source
  //   (9)
  //   (b)
  //   (d)
  //   I reg
  //   Instruction Pointer
  //   StacK pointer
  //   (8)
  //   (a)
  //   (e)
  //   DR/SP Select
  //   CLOCK
  //   DR Bank Select
  //   (f)
  //   IRQ Pending
  //   IRQ UnMASK
  //   ROM Write Enable
  //   (1)
  //   (2)
endmodule

module EUP51_Computer (
  input  HwIRQ,
  input  G,
  input  Stp,
  input  Rst,
  input  [6:0] KeyIn,
  input  KeyRdy,
  output Clk_o,
  output RS_o,
  output KeyAck
);

  wire Active_p2, and_1_out, and_2_out, button_1_out, controlled_buffer_2_out, controlled_buffer_4_out,
       d_ff_1_q, eup5108_1_p0oe, eup5108_1_p1l, keyboard_1_avail, not_1_out, not_2_out, or_1_out, or_2_out,
       or_3_out, or_4_out, pull_resistor_1_node, Reset_out, S1_out, StpGo_out;
  wire [6:0] keyboard_1_data;
  wire [7:0] controlled_buffer_3_out, eup5108_1_p1bo;
  wire [7:7] undriven, undriven_2;
  wire [23:0] counter_1_q;

  LED led_1 (.in(RS_o));
  Pull_Resistor pull_resistor_1 (.node(pull_resistor_1_node));
  // Switch SS: pin names not known; wires that end beside it: 1'b1, pull_resistor_1_node
  Button button_1 (.out(button_1_out));
  // Probe on counter_1_q
  Counter #(.max('hffffff), .width(24)) counter_1 (
    .Q(counter_1_q), .clk(Clk_o), .clr(button_1_out));  // open: load, D, count, carry, up
  Button S1 (.out(S1_out));
  or or_1 (or_1_out, S1_out, G);
  Button StpGo (.out(StpGo_out));
  or or_2 (or_2_out, StpGo_out, Stp);
  EUP5108 eup5108_1 (
    .P0el(d_ff_1_q), .P0oe(eup5108_1_p0oe), .P0es(controlled_buffer_2_out), .IRQ(not_1_out),
    .P0bi(controlled_buffer_3_out), .Step1(or_1_out), .Clk(Clk_o), .P1l(eup5108_1_p1l),
    .StopStart_i(or_2_out), .RS(RS_o), .Step1En_i(pull_resistor_1_node), .P1bo(eup5108_1_p1bo), .Rst(or_3_out));  // open: P0l, S_Cntl_In, P0bo, S_O, P1oe, P1el, P1es, P3bi, P3bo, P2oe, P1bi, P3es, P3l, P2l, P3el, P3oe, P2es, P2el, P2bi, P2bo
  Button Reset (.out(Reset_out));
  D_Flip_Flop d_ff_1 (
    .D(controlled_buffer_2_out), .clk(Clk_o), .Q(d_ff_1_q), .reset(eup5108_1_p0oe));  // open: Qn, preset
  or or_3 (or_3_out, Reset_out, Rst);
  assign KeyAck = not_2_out ? eup5108_1_p0oe : 1'bz;  // Controlled_Buffer controlled_buffer_1
  assign controlled_buffer_2_out = not_2_out ? and_1_out : 1'bz;  // Controlled_Buffer controlled_buffer_2
  assign controlled_buffer_3_out = not_2_out ? {undriven[7], KeyIn} : 8'bz;  // Controlled_Buffer controlled_buffer_3
  and and_1 (and_1_out, KeyRdy, ~KeyAck);  // AND_Gate
  not not_1 (not_1_out, HwIRQ);
  // Probe on controlled_buffer_3_out
  TTY #(.cols(80), .rows(25)) tty_1 (.data(eup5108_1_p1bo[6:0]), .clk(Clk_o), .we(eup5108_1_p1l), .clr(or_4_out));
  or or_4 (or_4_out, or_3_out, eup5108_1_p1bo[7]);
  not not_2 (not_2_out, Active_p2);
  assign controlled_buffer_4_out = Active_p2 ? eup5108_1_p0oe : 1'bz;  // Controlled_Buffer controlled_buffer_4
  Keyboard keyboard_1 (
    .clk(controlled_buffer_4_out), .re(1'b1), .avail(keyboard_1_avail), .data(keyboard_1_data));  // open: clr
  // Switch Active: pin names not known; wires that end beside it: 1'b1, Active_p2
  Pull_Resistor pull_resistor_2 (.node(Active_p2));
  assign controlled_buffer_2_out = Active_p2 ? and_2_out : 1'bz;  // Controlled_Buffer controlled_buffer_5
  and and_2 (and_2_out, keyboard_1_avail, ~controlled_buffer_4_out);  // AND_Gate
  assign controlled_buffer_3_out = Active_p2 ? {undriven_2[7], keyboard_1_data} : 8'bz;  // Controlled_Buffer controlled_buffer_6

  // Notes on the sheet:
  //   G: pull=down
  //   External Keyboard Interface
  //   Testing Terminal
  //   Internal Keyboard
endmodule

module Desktop_View (
);

  wire eup51_computer_1_keyack, eup51_computer_1_rs_o, G_out, keyboard_1_avail, Q_out, R_out, S_out;
  wire [6:0] keyboard_1_data;

  Button R (.out(R_out));
  Button S (.out(S_out));
  LED led_1 (.in(eup51_computer_1_rs_o));
  Button G (.out(G_out));
  EUP51_Computer eup51_computer_1 (
    .RS_o(eup51_computer_1_rs_o), .KeyAck(eup51_computer_1_keyack), .G(G_out), .Stp(S_out),
    .KeyIn(keyboard_1_data), .KeyRdy(keyboard_1_avail), .Rst(R_out), .HwIRQ(Q_out));  // open: Clk_o
  Keyboard keyboard_1 (
    .clk(eup51_computer_1_keyack), .re(eup51_computer_1_rs_o), .avail(keyboard_1_avail),
    .data(keyboard_1_data));  // open: clr
  Button Q (.out(Q_out));

  // Notes on the sheet:
  //   EUP51 System Console
endmodule

module PixelVideoDriver (
  input  Rst,
  input  [4:0] WriteAddr,
  input  [7:0] NewData,
  input  WriteEN,
  output [7:0] cols2,
  output [7:0] cols,
  output [31:0] rows
);

  wire and_1_out, clock_1_out, decoder_1_out0, decoder_1_out1, decoder_1_out2, decoder_1_out3, s_r_ff_1_q,
       s_r_ff_1_qn;
  wire [1:0] counter_1_q;
  wire [4:0] counter_2_q, multiplexer_1_out;
  wire [7:0] VIDEO_RAM_dout;

  Clock clock_1 (.out(clock_1_out));
  and and_1 (and_1_out, decoder_1_out3, ~s_r_ff_1_qn);  // AND_Gate
  Decoder #(.enable("false"), .select(2)) decoder_1 (
    .out0(decoder_1_out0), .out1(decoder_1_out1), .out2(decoder_1_out2), .out3(decoder_1_out3),
    .sel(counter_1_q));
  Counter #(.max('h3), .width(2)) counter_1 (
    .Q(counter_1_q), .clk(clock_1_out));  // open: load, D, count, carry, up, clr
  Counter #(.max('h1f), .width(5)) counter_2 (
    .Q(counter_2_q), .clk(decoder_1_out1));  // open: load, D, count, carry, up, clr
  S_R_Flip_Flop s_r_ff_1 (
    .S(WriteEN), .R(and_1_out), .clk(clock_1_out), .Q(s_r_ff_1_q), .Qn(s_r_ff_1_qn));  // open: reset, preset
  RAM #(.addrWidth(5), .asyncread("true"), .clearpin("true"), .\type ("nonvolatile")) VIDEO_RAM (
    .addr(multiplexer_1_out), .we(s_r_ff_1_q), .clk(decoder_1_out3), .din(NewData), .dout(VIDEO_RAM_dout),
    .clr(Rst));  // open: oe
  Multiplexer #(.enable("false"), .width(5)) multiplexer_1 (
    .in0(counter_2_q), .in1(WriteAddr), .out(multiplexer_1_out), .sel(decoder_1_out2));
  Decoder #(.enable("false"), .select(5)) decoder_2 (
    .out0(rows[31]), .out1(rows[30]), .out2(rows[29]), .out3(rows[28]), .out4(rows[27]), .out5(rows[26]),
    .out6(rows[25]), .out7(rows[24]), .out8(rows[23]), .out9(rows[22]), .out10(rows[21]), .out11(rows[20]),
    .out12(rows[19]), .out13(rows[18]), .out14(rows[17]), .out15(rows[16]), .out16(rows[15]),
    .out17(rows[14]), .out18(rows[13]), .out19(rows[12]), .out20(rows[11]), .out21(rows[10]),
    .out22(rows[9]), .out23(rows[8]), .out24(rows[7]), .out25(rows[6]), .out26(rows[5]), .out27(rows[4]),
    .out28(rows[3]), .out29(rows[2]), .out30(rows[1]), .out31(rows[0]), .sel(counter_2_q));
  Pull_Resistor pull_resistor_1 (.node({cols[0], cols[1], cols[2], cols[3], cols[4], cols[5], cols[6], cols[7]}));
  assign {cols[0], cols[1], cols[2], cols[3], cols[4], cols[5], cols[6], cols[7]} = decoder_1_out0 ? VIDEO_RAM_dout : 8'bz;  // Controlled_Buffer controlled_buffer_1
  // DotMatrix #(.inputtype("select"), .matrixcols(8), .matrixrows(32), .persist(256)) dotmatrix_1: pin names not known; wires that end beside it: cols, rows

  assign cols2 = {cols[0], cols[1], cols[2], cols[3], cols[4], cols[5], cols[6], cols[7]};

  // Notes on the sheet:
  //   Sequencer
  //   Row Counter
  //   Video RAM
  //   Row Select Decoder
endmodule

module LEDwMemory (
  input  [7:0] Di,
  input  Ld,
  input  Rst
);

  wire [3:0] register_1_q, register_1_q_2;

  Hex_Digit_Display #(.decimalPoint("false")) hex_digit_display_1 (.value(register_1_q_2));
  Hex_Digit_Display #(.decimalPoint("false")) hex_digit_display_2 (.value(register_1_q));
  Register #(.trigger("falling")) register_1 (
    .D(Di), .en(1'b1), .Q({register_1_q_2, register_1_q}), .clk(Ld), .clr(Rst));
endmodule

module EUP5109_DISPSYS (
  input  WriteEN,
  input  [7:0] DispData,
  input  [7:0] DispAddr,
  output [23:0] ColSelect,
  output [31:0] RowSelect
);

  wire and_1_out, and_2_out, and_3_out, and_4_out, and_5_out, and_6_out, and_7_out, decoder_1_out0,
       decoder_1_out1, decoder_1_out2;
  wire [4:0] decoder_1_out3;

  // Probe on DispAddr
  Decoder #(.enable("false"), .select(3)) decoder_1 (
    .out0(decoder_1_out0), .out1(decoder_1_out1), .out2(decoder_1_out2), .out3(decoder_1_out3[0]),
    .out4(decoder_1_out3[1]), .out5(decoder_1_out3[2]), .out6(decoder_1_out3[3]), .out7(decoder_1_out3[4]),
    .sel(DispAddr[7:5]));
  and and_1 (and_1_out, WriteEN, decoder_1_out0);
  and and_2 (and_2_out, WriteEN, decoder_1_out1);
  and and_3 (and_3_out, WriteEN, decoder_1_out2);
  PixelVideoDriver pixelvideodriver_1 (
    .cols(ColSelect[7:0]), .NewData(DispData), .WriteEN(and_1_out), .WriteAddr(DispAddr[4:0]),
    .Rst(decoder_1_out3[4]));  // open: cols2, rows
  PixelVideoDriver pixelvideodriver_2 (
    .cols(ColSelect[15:8]), .NewData(DispData), .WriteEN(and_2_out), .WriteAddr(DispAddr[4:0]),
    .Rst(decoder_1_out3[4]));  // open: cols2, rows
  PixelVideoDriver pixelvideodriver_3 (
    .cols(ColSelect[23:16]), .NewData(DispData), .WriteEN(and_3_out), .WriteAddr(DispAddr[4:0]),
    .Rst(decoder_1_out3[4]), .rows(RowSelect));  // open: cols2
  LEDwMemory ledwmemory_1 (.Rst(decoder_1_out3[4]), .Di(DispData), .Ld(and_4_out));
  // DotMatrix #(.inputtype("select"), .matrixcols(24), .matrixrows(32), .persist(256)) dotmatrix_1: pin names not known; wires that end beside it: ColSelect, RowSelect
  and and_4 (and_4_out, WriteEN, decoder_1_out3[3]);
  LEDwMemory ledwmemory_2 (.Rst(decoder_1_out3[4]), .Di(DispData), .Ld(and_5_out));
  and and_5 (and_5_out, WriteEN, decoder_1_out3[2]);
  and and_6 (and_6_out, WriteEN, decoder_1_out3[1]);
  LEDwMemory ledwmemory_3 (.Rst(decoder_1_out3[4]), .Di(DispData), .Ld(and_6_out));
  and and_7 (and_7_out, WriteEN, decoder_1_out3[0]);
  LEDwMemory ledwmemory_4 (.Rst(decoder_1_out3[4]), .Di(DispData), .Ld(and_7_out));

  // Notes on the sheet:
  //   0-8 0--32
  //   Chip Select
  //   Memory Map
  //   000 00000 - 000 11111 Left Band
  //   001 00000 - 001 11111 Center Band
  //   010 00000 - 010 11111 Right Band
  //   011 xxxxx - 011 xxxxx BCDD D
  //   100 xxxxx - 100 xxxxx BCDD C
  //   101 xxxxx - 101 xxxxx BCDD B
  //   110 xxxxx - 110 xxxxx BCDD A
  //   111 xxxxx - 111 xxxxx Reset
  //   Data Bus
  //   Address Bus
  //   Reset Line
  //   A          B   BCDD  C          D
  //   0
  //   32
endmodule

module GamingView (
);

  wire eup5108_1_p0l, eup5108_1_p2l, Go_out, not_1_out, or_1_out, Rst_out;
  wire [7:0] eup5108_1_p0bo, eup5108_1_p1bo, joystick_1_x;
  wire [23:0] dotmatrix_1_p2;
  wire [31:0] dotmatrix_1_p3;

  Button Go (.out(Go_out));
  not not_1 (not_1_out, Go_out);
  Button Rst (.out(Rst_out));
  EUP5108 eup5108_1 (
    .P0l(eup5108_1_p0l), .P0bo(eup5108_1_p0bo), .P1bo(eup5108_1_p1bo), .P2l(eup5108_1_p2l), .Rst(Rst_out),
    .P2es(1'b1), .P2el(or_1_out), .P2bi(joystick_1_x));  // open: P0el, S_Cntl_In, P0oe, P0es, IRQ, S_O, P1oe, P0bi, Step1, Clk, P1l, P1el, StopStart_i, RS, Step1En_i, P1es, P3bi, P3bo, P2oe, P1bi, P3es, P3l, P3el, P3oe, P2bo
  // DotMatrix #(.inputtype("select"), .matrixcols(24), .matrixrows(32), .persist(256)) dotmatrix_1: pin names not known; wires that end beside it: not_1_out, dotmatrix_1_p2, dotmatrix_1_p3
  or or_1 (or_1_out, eup5108_1_p2l, joystick_1_x[7], joystick_1_x[6], joystick_1_x[5], joystick_1_x[4]);
  Button button_1 (.out(joystick_1_x[7]));
  Button button_2 (.out(joystick_1_x[6]));
  EUP5109_DISPSYS eup5109_dispsys_1 (
    .DispAddr(eup5108_1_p1bo), .RowSelect(dotmatrix_1_p3), .DispData(eup5108_1_p0bo),
    .WriteEN(eup5108_1_p0l), .ColSelect(dotmatrix_1_p2));
  Joystick joystick_1 (.x(joystick_1_x[3:0]));  // open: y
  Button button_3 (.out(joystick_1_x[5]));
  Button button_4 (.out(joystick_1_x[4]));
endmodule

module basicmemory (
  input  [15:0] in_1,
  output [7:0] out_2,
  output [7:0] out_3
);

  wire button_1_out, pull_resistor_1_node;

  Pull_Resistor pull_resistor_1 (.node(pull_resistor_1_node));
  Button button_1 (.out(button_1_out));
  RAM #(.addrWidth(16), .databus("bidir")) ram_1 (
    .addr(in_1), .we(pull_resistor_1_node), .oe(1'b1), .clk(button_1_out), .data(out_2));

  assign out_3 = out_2;
endmodule
